# Fritzing sketch rgbrfid (saved by Fritzing 0.8.3b)
circuit board: 6.9215cm x 5.33756cm
breadboards: 1

parts:
  J1 = screw terminal, 8 pins
  Q1 = Basic FET P-Channel [package="TO220 [THT]"]
  Q2 = Basic FET P-Channel [package="TO220 [THT]"]
  Q3 = Basic FET P-Channel [package="TO220 [THT]"]
  Part1 = Arduino Uno (Rev3)
  J2 = female pin header, 4 pins [form="♀ (female)"]

nets:
  N1: J1.pin4, Q1.drain
  N2: J1.pin5, Q2.drain
  N3: J1.pin6, Q3.drain
  N4: J1.pin7, Q1.source, Q2.source, Q3.source, Part1.GND, J2.pin4
  N5: J1.pin8, Part1.VIN
  N6: Q1.gate, Part1.ICSP_MOSI, Part1.D11_PWM/MOSI
  N7: Q2.gate, Part1.D10_PWM/SS
  N8: Q3.gate, Part1.D9_PWM
  N9: Part1.D8, J2.pin3
  N10: Part1.D2, J2.pin2
  N11: Part1.5V, J2.pin1
