# Fritzing sketch rgbrfid2 (saved by Fritzing 0.8.3b)
circuit board: 6.88561cm x 5.36311cm
breadboards: 1

parts:
  RED = Basic FET P-Channel [package="TO220 [THT]"]
  GREEN = Basic FET P-Channel [package="TO220 [THT]"]
  BLUE = Basic FET P-Channel [package="TO220 [THT]"]
  LED = Screw terminal - 2 pins [package=THT]
  220 = Resistor [tolerance=±5% resistance=220 package=THT]
  J1 = screw terminal, 6 pins
  J2 = male pin header, 4 pins [form="♂ (male)"]
  BASBRUN_COM = Arduino Uno (Rev3)
  J3 = female pin header, 2 pins [form="♀ (female)"]

nets:
  N1: RED.gate, BASBRUN_COM.D5_PWM
  N2: RED.drain, J1.pin5
  N3: RED.source, BLUE.source
  N4: GREEN.gate, BASBRUN_COM.D6_PWM
  N5: GREEN.drain, J1.pin4
  N6: GREEN.source, LED.pin2, J1.pin1, J2.pin1, BASBRUN_COM.GND, J3.pin1
  N7: BLUE.gate, BASBRUN_COM.D3_PWM
  N8: BLUE.drain, J1.pin6
  N9: LED.pin1, 220.Pin_1
  N10: 220.Pin_0, BASBRUN_COM.D7
  N11: J1.pin2, J1.pin3, BASBRUN_COM.VIN
  N12: J2.pin2, BASBRUN_COM.D8
  N13: J2.pin3, BASBRUN_COM.D9_PWM
  N14: J2.pin4, BASBRUN_COM.5V
  N15: BASBRUN_COM.D10_PWM/SS, J3.pin2
